# Fritzing sketch 3.4 Lectura DS18B20 (saved by Fritzing 1.0.4)
breadboards: 1

parts:
  U1 = ESP32-38PinWide [part_number=ESP32-38PinWide]
  DS1 = DS18B20 1-Wire Temperature Sensor [part_number=DS18B20]
  R1 = Resistor [tolerance=±5% power=0.25W resistance=4700 package=THT]

nets:
  N1: U1.GPIO32, DS1.DQ, R1.Pin_1
  N2: U1.GPIO10, DS1.VDD, R1.Pin_0
  N3: U1.GPIO11, DS1.GND

custom parts:
  ESP32-38PinWide: Generic 38-Pin ESP32 with wide format (only access to one side of pins on a breadboard) based on Stephen Lilley's HiLetgo ESP-WROOM-32 ESP32 ESP-32S Development Board.
