# Fritzing sketch 3.4 Lectura NTC (saved by Fritzing 1.0.4)
breadboards: 1

parts:
  U1 = ESP32-38PinWide [part_number=ESP32-38PinWide]
  R2 = Temperature Sensor (Thermistor) [thermistor_type=NTC package=THT]
  R3 = Resistor [tolerance=±5% power=0.25W resistance=10000 package=THT]

nets:
  N1: U1.GPIO34, R2.pin_1, R3.Pin_1
  N2: U1.GPIO10, R3.Pin_0
  N3: U1.GPIO11, R2.pin_0

custom parts:
  ESP32-38PinWide: Generic 38-Pin ESP32 with wide format (only access to one side of pins on a breadboard) based on Stephen Lilley's HiLetgo ESP-WROOM-32 ESP32 ESP-32S Development Board.
