# Fritzing sketch 3.4 Visualizar OLED (saved by Fritzing 1.0.4)
breadboards: 1

parts:
  U1 = ESP32-38PinWide [part_number=ESP32-38PinWide]
  Grove1 = Grove OLED 128x96

nets:
  N1: U1.GPIO33, Grove1.SDA
  N2: U1.GPIO25, Grove1.SCL
  N3: U1.GPIO10, Grove1.VCC
  N4: U1.GPIO11, Grove1.GND

custom parts:
  ESP32-38PinWide: Generic 38-Pin ESP32 with wide format (only access to one side of pins on a breadboard) based on Stephen Lilley's HiLetgo ESP-WROOM-32 ESP32 ESP-32S Development Board.
